// Digital circuit addressing.dig as structural Verilog
module addressing (
  input  [7:0] PAGE,
  input  [7:0] X,
  input  [7:0] SP,
  input  [7:0] SPPS,
  input  [10:0] opr11,
  input  [7:0] opr8,
  input  [15:0] PC,
  input  [2:0] A_mode,
  output [7:0] D_out,
  output [15:0] A_out,
  output INH
);

  wire DIR, IMM, IND, or_1_out, or_2_out, or_3_out, or_4_out, REL, SP0, SP1;
  wire [15:0] add_1_s, bitextender_1_out, bitextender_2_out, driver_1_out, driver_4_out;

  Decoder #(.Selector_Bits(3)) decoder_1 (
    .sel(A_mode), .out_0(INH), .out_1(IMM), .out_2(DIR), .out_3(IND), .out_4(REL), .out_5(SP0), .out_6(SP1));  // open: out_7
  BitExtender #(.inputBits(11)) bitextender_1 (.in(opr11), .out(bitextender_1_out));
  BitExtender bitextender_2 (.in(opr8), .out(bitextender_2_out));
  or or_1 (or_1_out, SP0, SP1);
  or or_2 (or_2_out, IND, SP1);
  assign driver_1_out = IND ? {PAGE, X} : 16'bz;  // Driver driver_1
  assign driver_1_out = REL ? PC : 16'bz;  // Driver driver_2
  assign driver_1_out = or_1_out ? {SPPS, SP} : 16'bz;  // Driver driver_3
  assign driver_4_out = REL ? bitextender_1_out : 16'bz;  // Driver driver_4
  assign driver_4_out = or_2_out ? bitextender_2_out : 16'bz;  // Driver driver_5
  Add #(.Bits(16)) add_1 (.a(driver_1_out), .b(driver_4_out), .c_i(1'b0), .s(add_1_s));  // open: c_o
  or or_3 (or_3_out, SP0, or_2_out);
  or or_4 (or_4_out, REL, or_3_out);
  assign A_out = DIR ? {PAGE, opr8} : 16'bz;  // Driver driver_6
  assign A_out = or_4_out ? add_1_s : 16'bz;  // Driver driver_7
  assign D_out = IMM ? opr8 : 8'bz;  // Driver driver_8

  // Notes on the sheet:
  //   SPPS: Stack pointer page select
  //   opr11: 11-bit operand from instruction decoder
  //   opr8: 8-bit operand from instruction decoder
  //   A_mode: Addressing mode, from the CPU controller
  //   INH: Inharent addressing mode output
endmodule
