// Digital circuit alu.dig as structural Verilog
module alu (
  input  [7:0] ALU_0,
  input  [7:0] ALU_1,
  input  [4:0] OPC,
  input  C_i,
  input  ALU_r,
  input  CMP,
  output [7:0] D_o,
  output Z_o,
  output C_o
);

  wire ADD_c_o, and_1_out, decoder_1_out_1, decoder_1_out_2, decoder_1_out_3, decoder_1_out_4,
       decoder_1_out_9, decoder_1_out_10, or_1_out, or_2_out, SUBC_c_o;
  wire [0:0] or_3_out;
  wire [7:0] ADD_s, and_2_out, multiplexer_1_out, multiplexer_2_out, not_1_out, or_4_out, SUBC_s, xor_1_out;

  Decoder #(.Selector_Bits(4)) decoder_1 (
    .sel(OPC[3:0]), .out_1(decoder_1_out_1), .out_2(decoder_1_out_2), .out_3(decoder_1_out_3),
    .out_4(decoder_1_out_4), .out_9(decoder_1_out_9), .out_10(decoder_1_out_10));  // open: out_0, out_5, out_6, out_7, out_8, out_11, out_12, out_13, out_14, out_15
  or or_1 (or_1_out, decoder_1_out_1, decoder_1_out_3, decoder_1_out_9, decoder_1_out_10);
  or or_2 (or_2_out, decoder_1_out_2, decoder_1_out_4);
  and and_1 (and_1_out, C_i, or_1_out, ~CMP);  // And
  or or_3 (or_3_out[0], or_2_out, and_1_out);
  Multiplexer #(.Bits(8)) multiplexer_1 (.sel(or_2_out), .in_0(ALU_1), .in_1({8{1'b0}}), .out(multiplexer_1_out));
  Add #(.Bits(8)) ADD (.a(ALU_0), .b(multiplexer_1_out), .c_i(or_3_out[0]), .s(ADD_s), .c_o(ADD_c_o));
  Sub #(.Bits(8)) SUBC (.a(ALU_0), .b(multiplexer_1_out), .c_i(or_3_out[0]), .s(SUBC_s), .c_o(SUBC_c_o));
  assign and_2_out = ALU_0 & multiplexer_1_out;  // And and_2, 8 bits wide
  assign or_4_out = ALU_0 | multiplexer_1_out;  // Or or_4, 8 bits wide
  assign xor_1_out = ALU_0 ^ multiplexer_1_out;  // XOr xor_1, 8 bits wide
  assign not_1_out = ~ALU_0;  // Not not_1, 8 bits wide
  Multiplexer #(.Selector_Bits(4), .Bits(8)) multiplexer_2 (
    .sel(OPC[3:0]), .in_0(ADD_s), .in_1(ADD_s), .in_2(ADD_s), .in_3(SUBC_s), .in_4(SUBC_s), .in_5(and_2_out),
    .in_6(or_4_out), .in_7(xor_1_out), .in_8(not_1_out), .in_9({ALU_0[6:0], or_3_out[0]}),
    .in_10({or_3_out[0], ALU_0[7:1]}), .in_11({8{1'b0}}), .in_12({8{1'b0}}), .in_13({8{1'b0}}),
    .in_14({8{1'b0}}), .in_15({8{1'b0}}), .out(multiplexer_2_out));
  Multiplexer #(.Selector_Bits(4)) multiplexer_3 (
    .sel(OPC[3:0]), .in_0(ADD_c_o), .in_1(ADD_c_o), .in_2(ADD_c_o), .in_3(SUBC_c_o), .in_4(SUBC_c_o),
    .in_5(1'b0), .in_6(1'b0), .in_7(1'b0), .in_8(1'b0), .in_9(ALU_0[7]), .in_10(ALU_0[0]), .in_11(1'b0),
    .in_12(1'b0), .in_13(1'b0), .in_14(1'b0), .in_15(1'b0), .out(C_o));
  assign D_o = ALU_r ? multiplexer_2_out : 8'bz;  // Driver driver_1
  Comparator #(.Bits(8)) comparator_1 (.a(multiplexer_2_out), .b({8{1'b0}}), .eq(Z_o));  // open: gt, lt

  // Other names for the same wires on the sheet: sel[3:0] = OPC[3:0]

  // Notes on the sheet:
  //   C_i: Carry input
  //   D_o: Data output
  //   Z_o: Zero detect output
  //   C_o: Carry output
  //   CMP: Compare flag
  //   ROLC
  //   RORC
endmodule
