// Digital circuit control.dig as structural Verilog
module control (
  input  CLK,
  input  run,
  input  Z,
  input  C,
  input  [4:0] OPC,
  input  auto,
  output [2:0] cycle_o,
  output [22:0] control_o,
  output HLT,
  output PC_inc,
  output PC_rA,
  output PC_wA,
  output PC_rD,
  output PC_wD,
  output PC_HL,
  output RAM_r,
  output RAM_w,
  output IRH_w,
  output IRL_w,
  output [2:0] A_mode,
  output Rs_src,
  output Rd_w,
  output Rs_r,
  output SP_cnt,
  output SP_push,
  output ALU_r,
  output C_ctrl,
  output C_src,
  output END
);

  wire not_1_out, not_2_out, or_1_out;

  not not_1 (not_1_out, CLK);
  not not_2 (not_2_out, run);
  or or_1 (or_1_out, not_2_out, END);
  Counter #(.Bits(3)) Cycle (.en(run), .C(not_1_out), .clr(or_1_out), .out(cycle_o));  // open: ovf
  ROM #(.AddrBits(10), .Bits(23)) Control (.A({OPC, Z, C, cycle_o}), .sel(1'b1), .D(control_o));
  assign {HLT, PC_inc, PC_rA, PC_wA, PC_rD, PC_wD, PC_HL, RAM_r, RAM_w, IRH_w, IRL_w, A_mode, Rs_src, Rd_w, Rs_r, SP_cnt, SP_push, ALU_r, C_ctrl, C_src, END} = auto ? control_o : 23'bz;  // Driver driver_1

  // Notes on the sheet:
  //   auto: Set to 1 to use the program controller.
  //   0 is manual
  //   SP_cnt: Increment or decrement the stack pointer if this is high 
  //   on the next clock rising edge
  //   SP_push: Direction that stack pointer moves when SP_cnt is high
  //   1 = push on to stack
  //   0 = pull from stack
  //   C_ctrl: Force the Carry bit to this state
  //   C_src: The source that the Status register must use 
  //   for the Carry bit.
  //   0 = ALU
  //   1 = Controller
  //   END: End of the microcode routine
  //   contents of Control (hex, n*v repeats v):
  //   30a000,309000,400001,0,0,0,0,0,30a000,309000,400001,0,0,0,0,0,30a000,309000,400001,
  //   0,0,0,0,0,30a000,309000,400001,0,0,0,0,0,30a000,309000,281,0,0,0,0,0,30a000,309000,
  //   281,0,0,0,0,0,30a000,309000,281,0,0,0,0,0,30a000,309000,281,0,0,0,0,0,30a000,309000,
  //   8481,0,0,0,0,0,30a000,309000,8481,0,0,0,0,0,30a000,309000,8481,0,0,0,0,0,30a000,309000,
  //   8481,0,0,0,0,0,30a000,309000,8681,0,0,0,0,0,30a000,309000,8681,0,0,0,0,0,30a000,309000,
  //   8681,0,0,0,0,0,30a000,309000,8681,0,0,0,0,0,30a000,309000,8c81,0,0,0,0,0,30a000,309000,
  //   8c81,0,0,0,0,0,30a000,309000,8c81,0,0,0,0,0,30a000,309000,8c81,0,0,0,0,0,30a000,309000,
  //   4441,0,0,0,0,0,30a000,309000,4441,0,0,0,0,0,30a000,309000,4441,0,0,0,0,0,30a000,309000,
  //   4441,0,0,0,0,0,30a000,309000,4641,0,0,0,0,0,30a000,309000,4641,0,0,0,0,0,30a000,309000,
  //   4641,0,0,0,0,0,30a000,309000,4641,0,0,0,0,0,30a000,309000,4c41,0,0,0,0,0,30a000,309000,
  //   4c41,0,0,0,0,0,30a000,309000,4c41,0,0,0,0,0,30a000,309000,4c41,0,0,0,0,0,30a000,309000,
  //   1c1,0,0,0,0,0,30a000,309000,1c1,0,0,0,0,0,30a000,309000,1c1,0,0,0,0,0,30a000,309000,
  //   1c1,0,0,0,0,0,30a000,309000,80801,0,0,0,0,0,30a000,309000,80801,0,0,0,0,0,30a000,
  //   309000,80801,0,0,0,0,0,30a000,309000,80801,0,0,0,0,0,30a000,309000,801,0,0,0,0,0,
  //   30a000,309000,80801,0,0,0,0,0,30a000,309000,801,0,0,0,0,0,30a000,309000,80801,0,0,
  //   0,0,0,30a000,309000,80801,0,0,0,0,0,30a000,309000,801,0,0,0,0,0,30a000,309000,80801,
  //   0,0,0,0,0,30a000,309000,801,0,0,0,0,0,30a000,309000,801,0,0,0,0,0,30a000,309000,801,
  //   0,0,0,0,0,30a000,309000,80801,0,0,0,0,0,30a000,309000,80801,0,0,0,0,0,30a000,309000,
  //   80801,0,0,0,0,0,30a000,309000,80801,0,0,0,0,0,30a000,309000,801,0,0,0,0,0,30a000,
  //   309000,801,0,0,0,0,0,30a000,309000,54a30,44a30,80801,0,0,0,30a000,309000,54a30,44a30,
  //   80801,0,0,0,30a000,309000,54a30,44a30,80801,0,0,0,30a000,309000,54a30,44a30,80801,
  //   0,0,0,30a000,309000,28c20,38c21,0,0,0,0,30a000,309000,28c20,38c21,0,0,0,0,30a000,
  //   309000,28c20,38c21,0,0,0,0,30a000,309000,28c20,38c21,0,0,0,0,30a000,309000,189,0,
  //   0,0,0,0,30a000,309000,189,0,0,0,0,0,30a000,309000,189,0,0,0,0,0,30a000,309000,189,
  //   0,0,0,0,0,30a000,309000,189,0,0,0,0,0,30a000,309000,189,0,0,0,0,0,30a000,309000,189,
  //   0,0,0,0,0,30a000,309000,189,0,0,0,0,0,30a000,309000,189,0,0,0,0,0,30a000,309000,189,
  //   0,0,0,0,0,30a000,309000,189,0,0,0,0,0,30a000,309000,189,0,0,0,0,0,30a000,309000,189,
  //   0,0,0,0,0,30a000,309000,189,0,0,0,0,0,30a000,309000,189,0,0,0,0,0,30a000,309000,189,
  //   0,0,0,0,0,30a000,309000,189,0,0,0,0,0,30a000,309000,189,0,0,0,0,0,30a000,309000,189,
  //   0,0,0,0,0,30a000,309000,189,0,0,0,0,0,30a000,309000,189,0,0,0,0,0,30a000,309000,189,
  //   0,0,0,0,0,30a000,309000,189,0,0,0,0,0,30a000,309000,189,0,0,0,0,0,30a000,309000,189,
  //   0,0,0,0,0,30a000,309000,189,0,0,0,0,0,30a000,309000,189,0,0,0,0,0,30a000,309000,189,
  //   0,0,0,0,0,30a000,309000,189,0,0,0,0,0,30a000,309000,189,0,0,0,0,0,30a000,309000,189,
  //   0,0,0,0,0,30a000,309000,189,0,0,0,0,0,30a000,309000,189,0,0,0,0,0,30a000,309000,189,
  //   0,0,0,0,0,30a000,309000,189,0,0,0,0,0,30a000,309000,189,0,0,0,0,0,30a000,309000,189,
  //   0,0,0,0,0,30a000,309000,189,0,0,0,0,0,30a000,309000,189,0,0,0,0,0,30a000,309000,189,
  //   0,0,0,0,0,30a000,309000,3,0,0,0,0,0,30a000,309000,3,0,0,0,0,0,30a000,309000,3,0,0,
  //   0,0,0,30a000,309000,3,0,0,0,0,0,30a000,309000,7,0,0,0,0,0,30a000,309000,7,0,0,0,0,
  //   0,30a000,309000,7,0,0,0,0,0,30a000,309000,7,0,0,0,0,0,30a000,309000,4c71,0,0,0,0,
  //   0,30a000,309000,4c71,0,0,0,0,0,30a000,309000,4c71,0,0,0,0,0,30a000,309000,4c71,0,
  //   0,0,0,0,30a000,309000,8ca1,0,0,0,0,0,30a000,309000,8ca1,0,0,0,0,0,30a000,309000,8ca1,
  //   0,0,0,0,0,30a000,309000,8ca1,0,0,0,0,0,30a000,309000,1,0,0,0,0,0,30a000,309000,1,
  //   0,0,0,0,0,30a000,309000,1,0,0,0,0,0,30a000,309000,1,0,0,0,0,0,30a000,309000,1,0,0,
  //   0,0,0,30a000,309000,1,0,0,0,0,0,30a000,309000,1,0,0,0,0,0,30a000,309000,1
endmodule
