// Digital circuit cpu.dig as structural Verilog
module cpu (
  input  Clock,
  input  PC_inc,
  input  PC_rA,
  input  PC_wA,
  input  IRH_w,
  input  IRL_w,
  input  Rs_src,
  input  Rd_w,
  input  Rs_r,
  input  SP_cnt,
  input  SP_push,
  input  RAM_r,
  input  RAM_w,
  input  ALU_r,
  input  HLT,
  input  auto,
  input  run,
  input  C_ctrl,
  input  C_src,
  input  Clock_2,
  input  manual,
  input  [2:0] A_mode,
  input  PC_rD,
  input  PC_wD,
  input  PC_HL,
  output [2:0] Cycle_out,
  output [22:0] control_out,
  output [4:0] Opcode,
  output [15:0] PC,
  output [7:0] out_26,
  output [7:0] out_27,
  output [7:0] out_28,
  output [7:0] out_29,
  output [7:0] out_30,
  output END
);

  wire alu_1_c_o, alu_1_z_o, ALU_r_t, and_1_out, and_2_out, C_ctrl_t, C_src_t, CLK, comparator_1_lt,
       comparator_2_gt, HLT_t, INH, instruction_1_p10, IRH_w_t, IRL_w_t, multiplexer_1_out, or_1_out,
       PC_HL_t, PC_inc_t, PC_rA_t, PC_rD_t, PC_wA_t, PC_wD_t, RAM_r_t, RAM_w_t, Rd_w_t, Rs_r_t, Rs_src_t,
       run_t, SP_cnt_t, SP_push_t, status_1_c_o, status_1_z_o;
  wire [2:0] A_mode_t, instruction_1_p7, instruction_1_p8, instruction_1_p9;
  wire [7:0] instruction_1_p13, pc_1_d_out, registers_1_alu_0, registers_1_alu_1, registers_1_page,
       registers_1_sp, registers_1_x, SPPS;
  wire [10:0] instruction_1_p12;
  wire [15:0] pc_1_a_out;

  assign {C_src_t, C_ctrl_t, ALU_r_t, SP_push_t, SP_cnt_t, Rs_r_t, Rd_w_t, Rs_src_t, A_mode_t[0], A_mode_t[1], A_mode_t[2], IRL_w_t, IRH_w_t, RAM_w_t, RAM_r_t, PC_HL_t, PC_wD_t, PC_rD_t, PC_wA_t, PC_rA_t, PC_inc_t, HLT_t} = ~auto ? {C_src, C_ctrl, ALU_r, SP_push, SP_cnt, Rs_r, Rd_w, Rs_src, A_mode[0], A_mode[1], A_mode[2], IRL_w, IRH_w, RAM_w, RAM_r, PC_HL, PC_wD, PC_rD, PC_wA, PC_rA, PC_inc, HLT} : 22'bz;  // DriverInvSel driverinvsel_1
  Comparator #(.Bits(16)) comparator_1 (.a(pc_1_a_out), .b(16'h2), .lt(comparator_1_lt));  // open: gt, eq
  Comparator #(.Bits(16)) comparator_2 (.a(pc_1_a_out), .b(16'h5), .gt(comparator_2_gt));  // open: eq, lt
  pc pc_1 (
    .A_in(pc_1_a_out), .D_in(pc_1_d_out), .CLK(CLK), .run(run_t), .PC_inc(PC_inc_t), .PC_rA(PC_rA_t),
    .PC_wA(PC_wA_t), .PC_rD(PC_rD_t), .PC_wD(PC_wD_t), .PC_HL(PC_HL_t), .A_out(pc_1_a_out),
    .D_out(pc_1_d_out), .PC(PC));
  Multiplexer multiplexer_1 (.sel(manual), .in_0(Clock), .in_1(Clock_2), .out(multiplexer_1_out));
  or or_1 (or_1_out, comparator_1_lt, comparator_2_gt);
  and and_1 (and_1_out, RAM_w_t, or_1_out);
  and and_2 (and_2_out, or_1_out, RAM_r_t);
  and and_3 (CLK, multiplexer_1_out, ~HLT_t);  // And
  // instruction instruction_1: pin names not known; wires that end beside it: pc_1_d_out, CLK, IRH_w_t, IRL_w_t, Rs_src_t, INH, instruction_1_p7, instruction_1_p8, instruction_1_p9, instruction_1_p10, Opcode, instruction_1_p12, instruction_1_p13
  D_FF d_ff_1 (.D(run), .C(~CLK), .Q(run_t));  // open: nQ
  RAMSinglePort #(.AddrBits(16), .isProgramMemory("true"), .Bits(8)) ramsingleport_1 (
    .A(pc_1_a_out), .str(and_1_out), .C(CLK), .ld(and_2_out), .D(pc_1_d_out));
  peripherals peripherals_1 (
    .CLK(CLK), .RAM_w(RAM_w_t), .RAM_r(RAM_r_t), .D_in(pc_1_d_out), .A_in(pc_1_a_out), .SPPS(SPPS),
    .D_o(pc_1_d_out));
  registers registers_1 (
    .D_in(pc_1_d_out), .CLK(CLK), .R_d(instruction_1_p7), .Rd_w(Rd_w_t), .R_S0(instruction_1_p8),
    .R_S1(instruction_1_p9), .Rs_r(Rs_r_t), .nSt(instruction_1_p10), .SP_cnt(SP_cnt_t), .SP_push(SP_push_t),
    .D_out(pc_1_d_out), .ALU_0(registers_1_alu_0), .ALU_1(registers_1_alu_1), .A(out_26), .B(out_27),
    .C(out_28), .D(out_29), .E(out_30), .PAGE(registers_1_page), .X(registers_1_x), .SP(registers_1_sp));
  alu alu_1 (
    .ALU_0(registers_1_alu_0), .ALU_1(registers_1_alu_1), .OPC(Opcode), .C_i(status_1_c_o), .ALU_r(ALU_r_t),
    .D_o(pc_1_d_out), .Z_o(alu_1_z_o), .C_o(alu_1_c_o));  // open: CMP
  addressing addressing_1 (
    .PAGE(registers_1_page), .X(registers_1_x), .SP(registers_1_sp), .SPPS(SPPS), .opr11(instruction_1_p12),
    .opr8(instruction_1_p13), .PC(PC), .A_mode(A_mode_t), .D_out(pc_1_d_out), .A_out(pc_1_a_out), .INH(INH));
  status status_1 (
    .Z_alu(alu_1_z_o), .C_alu(alu_1_c_o), .ZC_w(ALU_r_t), .CLK(CLK), .C_ctrl(C_ctrl_t), .C_src(C_src_t),
    .Z_o(status_1_z_o), .C_o(status_1_c_o));
  control control_1 (
    .CLK(CLK), .run(run_t), .Z(status_1_z_o), .C(status_1_c_o), .OPC(Opcode), .auto(auto),
    .cycle_o(Cycle_out), .control_o(control_out), .HLT(HLT_t), .PC_inc(PC_inc_t), .PC_rA(PC_rA_t),
    .PC_wA(PC_wA_t), .PC_rD(PC_rD_t), .PC_wD(PC_wD_t), .PC_HL(PC_HL_t), .RAM_r(RAM_r_t), .RAM_w(RAM_w_t),
    .IRH_w(IRH_w_t), .IRL_w(IRL_w_t), .A_mode(A_mode_t), .Rs_src(Rs_src_t), .Rd_w(Rd_w_t), .Rs_r(Rs_r_t),
    .SP_cnt(SP_cnt_t), .SP_push(SP_push_t), .ALU_r(ALU_r_t), .C_ctrl(C_ctrl_t), .C_src(C_src_t), .END(END));

  // Notes on the sheet:
  //   Clock: Hz: 2
  //   Rd_w: Write to destination register
  //   Rs_r: Read from source register
  //   auto: Switch CPU control to auto (use controller)
  //   or control manually, default 1
endmodule
