// Digital circuit instruction.dig as structural Verilog
module instruction (
  input  [7:0] D_in,
  input  CLK,
  input  IRH_w,
  input  IRL_w,
  input  DIR8_sel,
  input  DIR11_sel,
  input  IMM_sel,
  input  Rs_src,
  output [15:0] A_out,
  output [7:0] D_out,
  output [2:0] R_d,
  output [2:0] R_S0,
  output [2:0] R_S1,
  output nSt,
  output [4:0] OPC
);

  wire or_1_out;
  wire [7:0] pulldown_1_out;
  wire [7:3] IR_L_q;

  Register #(.Bits(8)) IR_H (.D(D_in), .C(CLK), .en(IRH_w), .Q({OPC, R_d}));
  Register #(.Bits(8)) IR_L (.D(D_in), .C(CLK), .en(IRL_w), .Q({IR_L_q, R_S1}));
  PullDown #(.Bits(8)) pulldown_1 (.out(pulldown_1_out));
  Multiplexer #(.Bits(3)) multiplexer_1 (.sel(Rs_src), .in_0(R_d), .in_1(IR_L_q[6:4]), .out(R_S0));
  assign A_out = DIR11_sel ? {{5{1'b0}}, R_d, IR_L_q, R_S1} : 16'bz;  // Driver driver_1
  assign A_out = DIR8_sel ? {pulldown_1_out, IR_L_q, R_S1} : 16'bz;  // Driver driver_2
  assign D_out = IMM_sel ? {IR_L_q, R_S1} : 8'bz;  // Driver driver_3
  or or_1 (or_1_out, DIR11_sel, DIR8_sel, IMM_sel);
  and and_1 (nSt, IR_L_q[7], ~or_1_out);  // And

  // Notes on the sheet:
  //   D_in: Data bus input
  //   IRH_w: Write high byte of instruction register
  //   IRL_w: Write low byte of instruction register
  //   A_out: Direct address gated on to Address bus
  //   D_out: Immediate data gated on to Data bus
  //   nSt: Used to indicate whether a result should be
  //   written to R_d.
  //   Used for CMP, where we do an XOR, but don't write
  //   the result back to the register.
  //   DIR8_sel: 8-bit direct addressing mode
  //   Used for getting data to/from RAM in conjuction 
  //   with the PAGE register
  //   DIR11_sel: 11-bit direct addressing mode
  //   Used for branching
  //   OPC: Opcode output
  //   IMM_sel: Immediate mode
  //   Rs_src: Source register R_S0 can either be the first or 
  //   second operand, and this bit chooses which one.
  //   0=1st operand
  //   1=2nd operand
endmodule
