// Digital circuit pc.dig as structural Verilog
module pc (
  input  [15:0] A_in,
  input  [7:0] D_in,
  input  CLK,
  input  run,
  input  PC_inc,
  input  PC_rA,
  input  PC_wA,
  input  PC_rD,
  input  PC_wD,
  input  PC_HL,
  output [15:0] A_out,
  output [7:0] D_out,
  output [15:0] PC
);

  wire CLR, demultiplexer_1_out_0, demultiplexer_1_out_1, or_1_out, or_2_out, PC_L_ovf;
  wire [7:0] multiplexer_1_out, multiplexer_2_out, multiplexer_3_out;

  not not_1 (CLR, run);
  Demultiplexer demultiplexer_1 (.sel(PC_HL), .in(PC_wD), .out_0(demultiplexer_1_out_0), .out_1(demultiplexer_1_out_1));
  Multiplexer #(.Bits(8)) multiplexer_1 (.sel(PC_wA), .in_0(D_in), .in_1(A_in[15:8]), .out(multiplexer_1_out));
  Multiplexer #(.Bits(8)) multiplexer_2 (.sel(PC_wA), .in_0(D_in), .in_1(A_in[7:0]), .out(multiplexer_2_out));
  or or_1 (or_1_out, PC_wA, demultiplexer_1_out_1);
  or or_2 (or_2_out, demultiplexer_1_out_0, PC_wA);
  CounterPreset #(.Bits(8)) PC_H (
    .en(PC_L_ovf), .C(CLK), .dir(1'b0), .in(multiplexer_1_out), .ld(or_1_out), .clr(CLR), .out(PC[15:8]));  // open: ovf
  CounterPreset #(.Bits(8)) PC_L (
    .en(PC_inc), .C(CLK), .dir(1'b0), .in(multiplexer_2_out), .ld(or_2_out), .clr(CLR), .out(PC[7:0]),
    .ovf(PC_L_ovf));
  Multiplexer #(.Bits(8)) multiplexer_3 (.sel(PC_HL), .in_0(PC[7:0]), .in_1(PC[15:8]), .out(multiplexer_3_out));
  assign A_out = PC_rA ? PC : 16'bz;  // Driver driver_1
  assign D_out = PC_rD ? multiplexer_3_out : 8'bz;  // Driver driver_2

  // Notes on the sheet:
  //   A_in: Address bus input
  //   D_in: Data bus input
  //   CLK: Hz: 5
  //   PC_inc: Increment the lower byte of the program counter 
  //   on the next clock rising edge
  //   PC_rA: Read from Progeam Counter on to Address bus
  //   PC_wA: Write to program counter from address bus
  //   PC_rD: Read from Program Counter (H or L byte) 
  //   on to Data bus
  //   PC_wD: Write to high or low byte of program counter from data base.
  //   Choose byte to write using PC_HL
  //   PC_HL: Select the High or Low byte of the Program Counter
endmodule
