// Digital circuit peripherals.dig as structural Verilog
module peripherals (
  input  [15:0] A_in,
  input  [7:0] D_in,
  input  CLK,
  input  RAM_r,
  input  RAM_w,
  output [7:0] D_o,
  output [7:0] SPPS
);

  wire and_1_out, and_2_out, and_3_out, and_4_out, and_5_out, and_6_out, and_7_out, comparator_1_eq,
       comparator_2_eq, comparator_3_eq, comparator_4_eq, comparator_5_eq, RTC_L_ovf;
  wire [7:0] RTC_H_out, RTC_L_out;
  wire [15:8] input_d;

  Comparator #(.Bits(16)) comparator_1 (.a(A_in), .b(16'h2), .eq(comparator_1_eq));  // open: gt, lt
  Comparator #(.Bits(16)) comparator_2 (.a(A_in), .b(16'h3), .eq(comparator_2_eq));  // open: gt, lt
  Comparator #(.Bits(16)) comparator_3 (.a(A_in), .b(16'h4), .eq(comparator_3_eq));  // open: gt, lt
  Comparator #(.Bits(16)) comparator_4 (.a(A_in), .b(16'h5), .eq(comparator_4_eq));  // open: gt, lt
  Comparator #(.Bits(16)) comparator_5 (.a(A_in), .b(16'h6), .eq(comparator_5_eq));  // open: gt, lt
  and and_1 (and_1_out, comparator_1_eq, RAM_w);
  and and_2 (and_2_out, comparator_2_eq, RAM_w);
  and and_3 (and_3_out, comparator_3_eq, RAM_r);
  and and_4 (and_4_out, RAM_w, comparator_4_eq);
  and and_5 (and_5_out, comparator_4_eq, RAM_r);
  and and_6 (and_6_out, RAM_w, comparator_5_eq);
  and and_7 (and_7_out, comparator_5_eq, RAM_r);
  Register #(.Bits(8)) u_SPPS (.D(D_in), .C(CLK), .en(and_1_out), .Q(SPPS));
  Terminal \output  (.D(D_in), .C(CLK), .en(and_2_out));
  Keyboard \input  (.C(CLK), .en(and_3_out), .D({input_d, D_o}));  // open: av
  CounterPreset #(.Bits(8)) RTC_H (
    .en(RTC_L_ovf), .C(CLK), .dir(1'b0), .in(D_in), .ld(and_4_out), .clr(1'b0), .out(RTC_H_out));  // open: ovf
  CounterPreset #(.Bits(8)) RTC_L (
    .en(1'b1), .C(CLK), .dir(1'b0), .in(D_in), .ld(and_6_out), .clr(1'b0), .out(RTC_L_out), .ovf(RTC_L_ovf));
  assign D_o = and_5_out ? RTC_H_out : 8'bz;  // Driver driver_1
  assign D_o = and_7_out ? RTC_L_out : 8'bz;  // Driver driver_2

  // Notes on the sheet:
  //   SPPS: Stack pointer page select
endmodule
