// Digital circuit address modes.dig as structural Verilog
module address_modes (
  input  [10:0] opr11,
  input  [7:0] PAGE,
  input  [7:0] X,
  input  [15:0] PC,
  input  SP_push,
  input  clk,
  input  SP_cnt,
  input  SP_w,
  input  [7:0] opr8,
  input  [2:0] A_mode,
  input  [7:0] SPPS,
  output [15:0] Add16,
  output [7:0] Data8
);

  wire DIR, IMM, IND, or_1_out, or_2_out, REL, SP;
  wire [7:0] SP_out;
  wire [15:0] add_1_s, bitextender_1_out, bitextender_2_out, driver_2_out, driver_5_out;

  Decoder #(.Selector_Bits(3)) decoder_1 (
    .sel(A_mode), .out_1(IMM), .out_2(DIR), .out_3(IND), .out_4(REL), .out_5(SP));  // open: out_0, out_6, out_7
  assign Data8 = IMM ? opr8 : 8'bz;  // Driver driver_1
  CounterPreset #(.Bits(8)) u_SP (
    .en(SP_cnt), .C(clk), .dir(SP_push), .in(Data8), .ld(SP_w), .clr(1'b0), .out(SP_out));  // open: ovf
  BitExtender #(.inputBits(11)) bitextender_1 (.in(opr11), .out(bitextender_1_out));
  BitExtender bitextender_2 (.in(opr8), .out(bitextender_2_out));
  or or_1 (or_1_out, IND, SP);
  assign driver_2_out = IND ? {PAGE, X} : 16'bz;  // Driver driver_2
  assign driver_2_out = REL ? PC : 16'bz;  // Driver driver_3
  assign driver_2_out = SP ? {SPPS, SP_out} : 16'bz;  // Driver driver_4
  assign driver_5_out = REL ? bitextender_1_out : 16'bz;  // Driver driver_5
  assign driver_5_out = or_1_out ? bitextender_2_out : 16'bz;  // Driver driver_6
  Add #(.Bits(16)) add_1 (.a(driver_2_out), .b(driver_5_out), .c_i(1'b0), .s(add_1_s));  // open: c_o
  or or_2 (or_2_out, REL, or_1_out);
  assign Add16 = DIR ? {PAGE, opr8} : 16'bz;  // Driver driver_7
  assign Add16 = or_2_out ? add_1_s : 16'bz;  // Driver driver_8

  // Notes on the sheet:
  //   opr11: 11-bit operrand from instruction decoder
  //   opr8: 8-bit operrand from instruction decoder
  //   SPPS: Stack pointer page select
endmodule
