// Digital circuit dualcounter.dig as structural Verilog
module dualcounter (
  input  clk,
  input  cnt,
  input  SP_push,
  input  [1:0] in_H,
  input  [1:0] in_L,
  input  load,
  output [1:0] out_4,
  output [1:0] out_5
);

  wire H_ovf;

  CounterPreset #(.Bits(2)) H (
    .en(cnt), .C(clk), .dir(SP_push), .in(in_H), .ld(load), .clr(1'b0), .out(out_4), .ovf(H_ovf));
  CounterPreset #(.Bits(2)) L (
    .en(H_ovf), .C(clk), .dir(SP_push), .in(in_L), .ld(load), .clr(1'b0), .out(out_5));  // open: ovf
endmodule
