// Digital circuit signed adder.dig as structural Verilog
module signed_adder (
  input  [7:0] PC,
  input  [3:0] offset,
  output [7:0] PC_new,
  output overflow
);

  wire [7:0] bitextender_1_out;

  BitExtender #(.inputBits(4), .outputBits(8)) bitextender_1 (.in(offset), .out(bitextender_1_out));
  Add #(.Bits(8)) add_1 (.a(PC), .b(bitextender_1_out), .c_i(1'b0), .s(PC_new), .c_o(overflow));
endmodule
