// Digital circuit status.dig as structural Verilog
module status (
  input  Z_alu,
  input  C_alu,
  input  ZC_w,
  input  CLK,
  input  C_ctrl,
  input  C_src,
  output Z_o,
  output C_o
);

  wire multiplexer_1_out, or_1_out;

  Multiplexer multiplexer_1 (.sel(C_src), .in_0(C_alu), .in_1(C_ctrl), .out(multiplexer_1_out));
  or or_1 (or_1_out, ZC_w, C_src);
  Register Zero (.D(Z_alu), .C(CLK), .en(ZC_w), .Q(Z_o));
  Register Carry (.D(multiplexer_1_out), .C(CLK), .en(or_1_out), .Q(C_o));

  // Notes on the sheet:
  //   Z_alu: Zero bit from the ALU
  //   C_alu: Carry bit from the ALU
  //   Z_o: Zero output
  //   C_o: Carry output
  //   ZC_w: Write the Zero and Carry bit to registers.
  //   C_ctrl: Carry bit set by the CPU controller
  //   C_src: Source of the carry bit.
  //   0 = ALU
  //   1 = CPU controller
endmodule
